# Fritzing sketch WeatherCamSenzors (saved by Fritzing 0.9.9b)

parts:
  Grove1 = Grove OLED 128x96
  WeMos_D1_Mini1 = WeMos D1 Mini
  WeMos_D1_Mini_Protoboard_Shield1 = WeMos D1 Mini Protoboard Shield
  WeMos_D1_Mini_Micro_SD_Shield1 = WeMos D1 Mini Micro SD Shield
  TP1 = TP4056 [chip_label=TP4056 package="DIP (Dual Inline) [THT]"]
  M1 = BME280
  U1 = LIPO-110mAh [package=lipo-110]

nets:
  GND: Grove1.GND, WeMos_D1_Mini1.G, WeMos_D1_Mini_Protoboard_Shield1.G, WeMos_D1_Mini_Protoboard_Shield1.X4-Y5, WeMos_D1_Mini_Micro_SD_Shield1.G, TP1.pin6, M1.GND
  3V3: Grove1.VCC, WeMos_D1_Mini1.3V3, WeMos_D1_Mini_Protoboard_Shield1.3V3, WeMos_D1_Mini_Protoboard_Shield1.X2-Y8, WeMos_D1_Mini_Protoboard_Shield1.X3-Y5, WeMos_D1_Mini_Micro_SD_Shield1.3V3, TP1.pin3, M1.VIN
  N1: Grove1.SDA, WeMos_D1_Mini1.D2, WeMos_D1_Mini_Protoboard_Shield1.D2, WeMos_D1_Mini_Protoboard_Shield1.X6-Y5, M1.SDA
  N2: Grove1.SCL, WeMos_D1_Mini1.D1, WeMos_D1_Mini_Protoboard_Shield1.D1, WeMos_D1_Mini_Protoboard_Shield1.X5-Y5, M1.SCL
  N3: WeMos_D1_Mini1.D5, WeMos_D1_Mini_Micro_SD_Shield1.D5
  N4: WeMos_D1_Mini1.D6, WeMos_D1_Mini_Micro_SD_Shield1.D6
  N5: WeMos_D1_Mini1.D7, WeMos_D1_Mini_Micro_SD_Shield1.D7
  N6: WeMos_D1_Mini1.D8, WeMos_D1_Mini_Micro_SD_Shield1.D8
  N7: TP1.pin4, U1.+
  N8: TP1.pin5, U1.-

custom parts:
  TP4056: A DIP stand-in part for whatever IC you want. With 6 pins on a 300mil dual inline package (DIP) footprint.
  BME280: Temperature Humidity Barometric presure Sensor
